// Logisim project UniPC.circ as structural Verilog: 14 circuits, main circuit PC de 8 Bits
module PC_de_8_Bits (
  input  Arranque__0__Clock_manual
);

  wire and_1_out, clock_1_out, Clock_2_out, d_ff_1_q, Flag_Z_z, JMP_out, JZ_out, LOAD__D_out,
       multiplexer_1_out, or_1_out, Reset_out, STORE__D_out;
  wire [3:0] registro_autoincrementador_1_salida, registro_autoincrementador_1_salida_2;
  wire [7:0] ALU_salida, IR_q, multiplexer_2_out, multiplexer_3_out, ram_1_data, Registro_AC_q;
  wire [15:8] IR_q_2, ram_1_data_2;

  Clock clock_1 (.out(clock_1_out));
  Button Clock_2 (.out(Clock_2_out));
  Multiplexer multiplexer_1 (
    .in0(Clock_2_out), .in1(clock_1_out), .out(multiplexer_1_out), .sel(Arranque__0__Clock_manual));  // open: en
  Button Reset (.out(Reset_out));
  Hex_Digit_Display hex_digit_display_1 (.value(registro_autoincrementador_1_salida_2));  // open: dp
  Hex_Digit_Display hex_digit_display_2 (.value(registro_autoincrementador_1_salida));  // open: dp
  Registro_Autoincrementador registro_autoincrementador_1 (
    .DEST_JMP(ram_1_data), .Clock(multiplexer_1_out), .Reset(Reset_out), .JMP(JMP_out),
    .Salida({registro_autoincrementador_1_salida_2, registro_autoincrementador_1_salida}));
  Multiplexer #(.width(8)) multiplexer_2 (
    .in0({registro_autoincrementador_1_salida_2, registro_autoincrementador_1_salida}), .in1(IR_q),
    .out(multiplexer_2_out), .sel(or_1_out));  // open: en
  or JMP (JMP_out, ram_1_data_2[15], JZ_out);
  or or_1 (or_1_out, LOAD__D_out, and_1_out);
  and LOAD__D (LOAD__D_out, multiplexer_1_out, IR_q_2[13]);
  and and_1 (and_1_out, multiplexer_1_out, d_ff_1_q);
  and JZ (JZ_out, ram_1_data_2[14], Flag_Z_z);
  and STORE__D (STORE__D_out, multiplexer_1_out, d_ff_1_q);
  RAM #(.dataWidth(16), .bus("separate")) ram_1 (
    .addr(multiplexer_2_out), .din({{8{1'b0}}, Registro_AC_q}), .data({ram_1_data_2, ram_1_data}),
    .clk(STORE__D_out));  // open: str, sel, ld, clr
  Register #(.width(16)) IR (
    .D({ram_1_data_2, ram_1_data}), .Q({IR_q_2, IR_q}), .clk(multiplexer_1_out), .clr(Reset_out));  // open: en
  D_Flip_Flop d_ff_1 (
    .clk(multiplexer_1_out), .D(IR_q_2[11]), .Q(d_ff_1_q), .reset(Reset_out));  // open: Qn, preset, en
  Hex_Digit_Display hex_digit_display_3 (.value(IR_q_2[15:12]));  // open: dp
  Multiplexer #(.width(8)) multiplexer_3 (
    .in0(ram_1_data), .in1(IR_q), .out(multiplexer_3_out), .sel(IR_q_2[12]));  // open: en
  ALU_de_8_Bits ALU (
    .Load_B__111____Suma__011____Resta__100____AND__001____OR__010____MUL2__101(IR_q_2[10:8]),
    .A(Registro_AC_q), .B(multiplexer_3_out), .Salida(ALU_salida));  // open: Carry
  Hex_Digit_Display hex_digit_display_4 (.value(IR_q[7:4]));  // open: dp
  Hex_Digit_Display hex_digit_display_5 (.value(IR_q_2[11:8]));  // open: dp
  Hex_Digit_Display hex_digit_display_6 (.value(Registro_AC_q[3:0]));  // open: dp
  Hex_Digit_Display hex_digit_display_7 (.value(Registro_AC_q[7:4]));  // open: dp
  Register #(.trigger("falling")) Registro_AC (
    .D(ALU_salida), .Q(Registro_AC_q), .clk(multiplexer_1_out), .clr(Reset_out));  // open: en
  Comparador_Con_Cero_8_Bits Flag_Z (.IN(Registro_AC_q), .Z(Flag_Z_z));
  Hex_Digit_Display hex_digit_display_8 (.value(IR_q[3:0]));  // open: dp

  // Notes on the sheet:
  //   Contador de Programa
  //   UniPC
  //   Memoria RAM
  //   Dato a almacenar en RAM
  //   Instr. Pre cargada
  //   Instr. Decod. (Operando 8b)
  //   Sel. Modo Direcc.
  //   Instrucción
  //   ACUMULADOR
endmodule

module Sumador_Simple_1_Bit (
  input  A,
  input  B,
  output C,
  output S
);

  and and_1 (C, A, B);
  xor xor_1 (S, A, B);
endmodule

module Sumador_Completo_1_Bit (
  input  A,
  input  B,
  input  Cin,
  output Cout,
  output S
);

  wire sumador_simple_1_bit_1_c, sumador_simple_1_bit_1_s, sumador_simple_1_bit_2_c;

  or or_1 (Cout, sumador_simple_1_bit_1_c, sumador_simple_1_bit_2_c);
  Sumador_Simple_1_Bit sumador_simple_1_bit_1 (
    .C(sumador_simple_1_bit_1_c), .A(B), .B(Cin), .S(sumador_simple_1_bit_1_s));
  Sumador_Simple_1_Bit sumador_simple_1_bit_2 (
    .C(sumador_simple_1_bit_2_c), .A(A), .B(sumador_simple_1_bit_1_s), .S(S));
endmodule

module Sumador_8_Bits (
  input  [7:0] A,
  input  [7:0] B,
  output Cout,
  output [7:0] S
);

  wire sumador_completo_1_bit_2_cout, sumador_completo_1_bit_3_cout, sumador_completo_1_bit_4_cout,
       sumador_completo_1_bit_5_cout, sumador_completo_1_bit_6_cout, sumador_completo_1_bit_7_cout,
       sumador_simple_1_bit_1_c;

  Sumador_Completo_1_Bit sumador_completo_1_bit_1 (
    .Cout(Cout), .A(A[7]), .B(B[7]), .Cin(sumador_completo_1_bit_2_cout), .S(S[7]));
  Sumador_Completo_1_Bit sumador_completo_1_bit_2 (
    .Cout(sumador_completo_1_bit_2_cout), .A(A[6]), .B(B[6]), .Cin(sumador_completo_1_bit_3_cout), .S(S[6]));
  Sumador_Completo_1_Bit sumador_completo_1_bit_3 (
    .Cout(sumador_completo_1_bit_3_cout), .A(A[5]), .B(B[5]), .Cin(sumador_completo_1_bit_4_cout), .S(S[5]));
  Sumador_Completo_1_Bit sumador_completo_1_bit_4 (
    .Cout(sumador_completo_1_bit_4_cout), .A(A[4]), .B(B[4]), .Cin(sumador_completo_1_bit_5_cout), .S(S[4]));
  Sumador_Completo_1_Bit sumador_completo_1_bit_5 (
    .Cout(sumador_completo_1_bit_5_cout), .A(A[3]), .B(B[3]), .Cin(sumador_completo_1_bit_7_cout), .S(S[3]));
  Sumador_Completo_1_Bit sumador_completo_1_bit_6 (
    .Cout(sumador_completo_1_bit_6_cout), .A(A[1]), .B(B[1]), .Cin(sumador_simple_1_bit_1_c), .S(S[1]));
  Sumador_Completo_1_Bit sumador_completo_1_bit_7 (
    .Cout(sumador_completo_1_bit_7_cout), .A(A[2]), .B(B[2]), .Cin(sumador_completo_1_bit_6_cout), .S(S[2]));
  Sumador_Simple_1_Bit sumador_simple_1_bit_1 (.C(sumador_simple_1_bit_1_c), .A(A[0]), .B(B[0]), .S(S[0]));
endmodule

module Inversor_8_bits (
  input  [7:0] IN,
  output [7:0] OUT
);

  assign OUT = ~IN;  // NOT_Gate not_1, 8 bits wide
endmodule

module Incrementador_8_bits (
  input  [7:0] A,
  output [7:0] S
);

  Sumador_8_Bits Sumador_8_Bits (.A(A), .B(8'h1), .S(S));  // open: Cout
endmodule

module Inverso_Aditivo_8_bits (
  input  [7:0] IN,
  output [7:0] OUT
);

  wire [7:0] Inversor_8_Bits_out;

  Inversor_8_bits Inversor_8_Bits (.IN(IN), .OUT(Inversor_8_Bits_out));
  Incrementador_8_bits Incrementador_8_Bits (.A(Inversor_8_Bits_out), .S(OUT));
endmodule

module Restador_8_bits (
  input  [7:0] A,
  input  [7:0] B,
  output [7:0] OUT
);

  wire [7:0] Inv__Aditivo_out;

  Sumador_8_Bits sumador_8_bits_1 (.A(A), .B(Inv__Aditivo_out), .S(OUT));  // open: Cout
  Inverso_Aditivo_8_bits Inv__Aditivo (.IN(B), .OUT(Inv__Aditivo_out));
endmodule

module Comparador_Con_Cero_8_Bits (
  input  [7:0] IN,
  output Z
);

  and and_1 (Z, ~IN[7], ~IN[6], ~IN[5], ~IN[4], ~IN[2], ~IN[1], ~IN[0], ~IN[3]);  // AND_Gate
endmodule

// N
module Negativo_N (
  input  [7:0] A,
  output N
);


  assign N = A[7];
endmodule

// V
module Overflow_V (
  input  [7:0] A,
  input  [7:0] B,
  input  [7:0] S,
  output V
);

  wire and_1_out, and_2_out;

  and and_1 (and_1_out, A[7], B[7], ~S[7]);  // AND_Gate
  and and_2 (and_2_out, ~A[7], ~B[7], S[7]);  // AND_Gate
  xor xor_1 (V, and_1_out, and_2_out);
endmodule

module ALU_de_8_Bits (
  input  [7:0] A,
  input  [7:0] B,
  input  [2:0] Load_B__111____Suma__011____Resta__100____AND__001____OR__010____MUL2__101,
  output Carry,
  output [7:0] Salida
);

  wire [7:0] AND_8_Bits_out, MultiplicadorX2_8_Bits_out_2, OR_8_Bits_out, Restador_8_bits_out,
       Sumador_8_bits_s;

  assign AND_8_Bits_out = A & B;  // AND_Gate AND_8_Bits, 8 bits wide
  assign OR_8_Bits_out = A | B;  // OR_Gate OR_8_Bits, 8 bits wide
  Sumador_8_Bits Sumador_8_bits (.Cout(Carry), .A(A), .B(B), .S(Sumador_8_bits_s));
  Multiplexer #(.select(3), .width(8)) multiplexer_1 (
    .in1(AND_8_Bits_out), .in2(OR_8_Bits_out), .in3(Sumador_8_bits_s), .in4(Restador_8_bits_out),
    .in5(MultiplicadorX2_8_Bits_out_2), .in7(B), .out(Salida),
    .sel(Load_B__111____Suma__011____Resta__100____AND__001____OR__010____MUL2__101));  // open: in0, in6, en
  Restador_8_bits Restador_8_bits (.A(A), .B(B), .OUT(Restador_8_bits_out));
  MultiplicadorX2_8_bits MultiplicadorX2_8_Bits (.IN(A), .out_2(MultiplicadorX2_8_Bits_out_2));
endmodule

// PC
module Registro_Autoincrementador (
  input  [7:0] DEST_JMP,
  input  Clock,
  input  Reset,
  input  JMP,
  output [7:0] Salida
);

  wire [7:0] multiplexer_1_out, sumador_8_bits_1_s;

  Multiplexer #(.width(8)) multiplexer_1 (
    .in0(sumador_8_bits_1_s), .in1(DEST_JMP), .out(multiplexer_1_out), .sel(JMP));  // open: en
  Sumador_8_Bits sumador_8_bits_1 (.A(Salida), .B(8'h1), .S(sumador_8_bits_1_s));  // open: Cout
  Register register_1 (.D(multiplexer_1_out), .Q(Salida), .clk(Clock), .clr(Reset));  // open: en
endmodule

module MultiplicadorX2_8_bits (
  input  [7:0] IN,
  output [7:0] out_2
);


  assign out_2 = {IN[6:0], 1'b0};
endmodule
